# Fritzing sketch OurProject (saved by Fritzing 0.9.3b)
breadboards: 1

parts:
  J1 = Basic Servo
  부품1 = Arduino Uno (Rev3)
  R1 = Photocell (LDR) [package=THT]
  R2 = Resistor [tolerance=±5% resistance=10k package=THT]
  R3 = Resistor [tolerance=±5% resistance=330 package=THT]
  R4 = Resistor [tolerance=±5% resistance=330 package=THT]
  R6 = Resistor [tolerance=±5% resistance=330 package=THT]
  J2 = Piezo Speaker
  LED1 = RGB LED (com. cathode, rgb) [package="5 mm [THT]"]

nets:
  GND: J1.gnd, 부품1.GND, R1.pin_1, J2.pin1, LED1.common_cathode
  VCC: J1.vcc, 부품1.5V, R2.Pin_1
  N1: J1.pulse, 부품1.D4
  N2: 부품1.A0, R1.pin_0, R2.Pin_0
  N3: 부품1.D9_PWM, R3.Pin_1
  N4: 부품1.D10_PWM/SS, R4.Pin_1
  N5: 부품1.D11_PWM/MOSI, R6.Pin_1
  N6: 부품1.D6_PWM, J2.pin2
  N7: R3.Pin_0, LED1.red_anode
  N8: R4.Pin_0, LED1.green_anode
  N9: R6.Pin_0, LED1.blue_anode
